# Fritzing sketch Schematic (saved by Fritzing 0.9.3b)
breadboards: 1

parts:
  U1 = ESP32-38PinWide [part_number=ESP32-38PinWide]
  Part1 = FTDI Basic Programmer
  C1 = Capacitor Polarized [package=cpol-radial-10uf-25v]

nets:
  N1: U1.EN, C1.+
  GND: U1.GND, Part1.GND
  N2: U1.GPIO11, C1.-
  N3: U1.GPIO16, Part1.TXO
  N4: U1.GPIO17, Part1.RXI

custom parts:
  ESP32-38PinWide: Generic 38-Pin ESP32 with wide format (only access to one side of pins on a breadboard) based on Stephen Lilley's HiLetgo ESP-WROOM-32 ESP32 ESP-32S Development Board.
